# Fritzing sketch prototype (saved by Fritzing 1.0.6)
breadboards: 1

parts:
  A1 = Raspberry Pi Pico2
  Part1 = Adafruit SDIO microSD Breakout
  JP1 = Header 8 [package=1x08_smd]

nets:
  N1: A1.pin_2, JP1.8
  N2: A1.pin_3, A1.pin_8, A1.pin_13, A1.pin_18, A1.pin_23, A1.pin_28, A1.pin_33, A1.pin_38, Part1.GND, JP1.2
  N3: A1.pin_4, JP1.5
  N4: A1.pin_11, JP1.6
  N5: A1.pin_12, JP1.7
  N6: A1.pin_14, Part1.SCLK, JP1.4
  N7: A1.pin_15, Part1.DI, JP1.3
  N8: A1.pin_16, Part1.DO
  N9: A1.pin_20, Part1.CS
  N10: A1.pin_36, Part1.3.3V, JP1.1

notes:
  Header pinout
  8 - GP1 - BUSY
  7 - GP9 - RST
  6 - GP8 - DC
  5 - GP2 - CS
  4 - GP10 - CLK
  3 - GP 11 - MOSI
  2 - GND
  1 - VCC
  8 - GP1 - BUSY (left)
  7 - GP9 - RST
  6 - GP8 - DC
  5 - GP2 - CS
  4 - GP10 - CLK
  3 - GP 11 - MOSI
  2 - GND
  1 - VCC (right)

custom parts:
  Raspberry Pi Pico2: Raspberry Pi Pico 2 is our new $5 microcontroller board, built on RP2350: our new high-performance, secure microcontroller.
